// Logisim project recicladora.circ as structural Verilog: 1 circuit, main circuit main
module main (
  input  _1,
  input  _2,
  input  _4,
  input  vidrio,
  input  _8,
  input  papel,
  input  organico
);

  wire and_1_out, and_2_out, and_3_out, and_4_out, and_5_out, or_1_out, or_2_out;

  and and_1 (and_1_out, vidrio, _2, _8);
  and and_2 (and_2_out, papel, _1, _4);
  and and_3 (and_3_out, organico, _4, _8);
  // Probe on or_2_out
  and and_4 (and_4_out, ~_1, ~_2, ~_4, ~_8);  // AND_Gate
  or or_1 (or_1_out, _8, _4, _2, _1);
  and and_5 (and_5_out, or_1_out, ~or_2_out);  // AND_Gate
  or or_2 (or_2_out, and_1_out, and_2_out, and_3_out);
  LED led_1 (.in(and_4_out));
  LED led_2 (.in(and_5_out));
  LED led_3 (.in(or_2_out));

  // Notes on the sheet:
  //   BCD TO BINARIO
  //   Estado del cilindro 
  //   Standby
  //   recibiendo carga
  //   Vaciar tolva
endmodule
